# Fritzing sketch Geo-Color Bot wiring diagram (saved by Fritzing 0.9.3b)
breadboards: 1

parts:
  Componente1 = Arduino Mega 2560 (Rev3)
  HC-SR04_Sensor_1 = HC-SR04 Ultrasonic Distance Sensor
  Componente2 = Motor Driver 1A Dual TB6612FNG
  HC-SR04_Sensor_2 = HC-SR04 Ultrasonic Distance Sensor
  HC-SR04_Sensor_3 = HC-SR04 Ultrasonic Distance Sensor
  HC-SR04_Sensor_4 = HC-SR04 Ultrasonic Distance Sensor
  M1 = DC Motor
  M2 = DC Motor
  VCC2 = Battery

nets:
  N1: Componente1.A0, Componente2.PWMA
  N2: Componente1.A1, Componente2.AIN2
  N3: Componente1.A2, Componente2.AIN1
  N4: Componente1.A4, Componente2.BIN1
  N5: Componente1.A5, Componente2.BIN2
  N6: Componente1.A6, Componente2.PWMB
  GND: Componente1.GND, HC-SR04_Sensor_1.GND, Componente2.GND, HC-SR04_Sensor_2.GND, HC-SR04_Sensor_3.GND, HC-SR04_Sensor_4.GND, VCC2.-
  N7: Componente1.RESET, Componente2.STBY
  VCC: Componente1.5V, HC-SR04_Sensor_1.VCC, Componente2.VCC, HC-SR04_Sensor_2.VCC, HC-SR04_Sensor_3.VCC, HC-SR04_Sensor_4.VCC
  N8: Componente1.VIN, Componente2.VM, VCC2.+
  N9: Componente1.D22, HC-SR04_Sensor_1.ECHO
  N10: Componente1.D23, HC-SR04_Sensor_1.TRIG
  N11: Componente1.D24, HC-SR04_Sensor_2.ECHO
  N12: Componente1.D25, HC-SR04_Sensor_2.TRIG
  N13: Componente1.D26, HC-SR04_Sensor_3.ECHO
  N14: Componente1.D27, HC-SR04_Sensor_3.TRIG
  N15: Componente1.D28, HC-SR04_Sensor_4.ECHO
  N16: Componente1.D29, HC-SR04_Sensor_4.TRIG
  N17: Componente2.B01, M2.pin_2
  N18: Componente2.B02, M2.pin_1
  N19: Componente2.A02, M1.pin_2
  N20: Componente2.A01, M1.pin_1

notes:
  Pines del TCS3200
  (Sensor de Color)
  GND
  LED
  S0
  S1
  VCC
  GND
  OUT
  S2
  S3
  VCC
